// Digital circuit TDM_4_7Segment.dig as structural Verilog
module TDM_4_7Segment (
  input  clk,
  output digit_4,
  output digit_3,
  output digit_2,
  output digit_1
);

  wire decoder_2_out_3;
  wire [1:0] counter_1_out;
  wire [3:0] multiplexer_1_out;

  Counter #(.Bits(2)) counter_1 (.en(1'b1), .C(clk), .clr(decoder_2_out_3), .out(counter_1_out));  // open: ovf
  Multiplexer #(.Bits(4), .Selector_Bits(2)) multiplexer_1 (
    .sel(counter_1_out), .in_0(4'b1001), .in_1(4'b1000), .in_2(4'b0111), .in_3(4'b0110),
    .out(multiplexer_1_out));
  Decoder #(.Selector_Bits(2)) decoder_1 (
    .sel(counter_1_out), .out_0(digit_4), .out_1(digit_3), .out_2(digit_2), .out_3(digit_1));
  Decoder #(.Selector_Bits(2)) decoder_2 (.sel(counter_1_out), .out_3(decoder_2_out_3));  // open: out_0, out_1, out_2
  Seven_Seg_Hex seven_seg_hex_1 (.d(multiplexer_1_out), .dp(1'b0));
  Seven_Seg_Hex seven_seg_hex_2 (.d(multiplexer_1_out), .dp(1'b0));
  Seven_Seg_Hex seven_seg_hex_3 (.d(multiplexer_1_out), .dp(1'b0));
  Seven_Seg_Hex seven_seg_hex_4 (.d(multiplexer_1_out), .dp(1'b0));

  // Notes on the sheet:
  //   clk: Hz: 1000
  //   Digit Data MUX
  //   Digit Enable Decoder
  //   Note : 
  //   There is no enable pin for this
  //    7 segment model thus display
  //   TDM cannot be well shown.
  //   But you can see at digit enable
  //   decoder that this circuit functions
  //   as it was designed to.
endmodule
